// Logisim project ALU(16 bit counter).circ as structural Verilog: 1 circuit, main circuit main
module main (
  input  CLR,
  input  Load,
  input  INR,
  input  I0,
  input  I1,
  input  I2,
  input  I3,
  input  I4,
  input  I5,
  input  I6,
  input  I7,
  input  I8,
  input  I9,
  input  I10,
  input  I11,
  input  I12,
  input  I13,
  input  I14,
  input  I15,
  input  Clock,
  input  Enable,
  output AC0,
  output AC1,
  output AC2,
  output AC3,
  output AC4,
  output AC5,
  output AC6,
  output AC7,
  output AC8,
  output AC9,
  output AC10,
  output AC11,
  output AC12,
  output AC13,
  output AC14,
  output AC15,
  output output_carry
);

  wire and_1_out, and_2_out, and_3_out, and_4_out, and_5_out, and_6_out, and_7_out, and_8_out, and_9_out,
       and_10_out, and_11_out, and_12_out, and_13_out, and_14_out, and_15_out, and_16_out, and_17_out,
       and_18_out, and_19_out, and_20_out, and_21_out, and_22_out, and_23_out, and_24_out, and_25_out,
       and_26_out, and_27_out, and_28_out, and_29_out, and_30_out, and_31_out, and_32_out, and_33_out,
       and_34_out, and_35_out, and_36_out, and_37_out, and_38_out, and_39_out, and_40_out, and_41_out,
       and_42_out, and_43_out, and_44_out, and_45_out, and_46_out, and_47_out, and_48_out, and_49_out,
       not_1_out, not_2_out, not_3_out, not_4_out, not_5_out, not_6_out, not_7_out, not_8_out, not_9_out,
       not_10_out, not_11_out, not_12_out, not_13_out, not_14_out, not_15_out, not_16_out, not_17_out,
       not_18_out, or_1_out, or_2_out, or_3_out, or_4_out, or_5_out, or_6_out, or_7_out, or_8_out, or_9_out,
       or_10_out, or_11_out, or_12_out, or_13_out, or_14_out, or_15_out, or_16_out, or_17_out, or_18_out,
       or_19_out, or_20_out, or_21_out, or_22_out, or_23_out, or_24_out, or_25_out, or_26_out, or_27_out,
       or_28_out, or_29_out, or_30_out, or_31_out, or_32_out;

  not not_1 (not_1_out, I0);
  not not_2 (not_2_out, I1);
  not not_3 (not_3_out, I2);
  not not_4 (not_4_out, I3);
  not not_5 (not_5_out, I4);
  not not_6 (not_6_out, I5);
  not not_7 (not_7_out, I6);
  not not_8 (not_8_out, I7);
  not not_9 (not_9_out, I8);
  not not_10 (not_10_out, I9);
  not not_11 (not_11_out, I10);
  not not_12 (not_12_out, I11);
  not not_13 (not_13_out, I12);
  not not_14 (not_14_out, I13);
  not not_15 (not_15_out, I14);
  not not_16 (not_16_out, I15);
  not not_17 (not_17_out, CLR);
  not not_18 (not_18_out, Load);
  and and_1 (and_1_out, not_17_out, Load);
  and and_2 (and_2_out, not_17_out, not_18_out, INR);
  and and_3 (and_3_out, and_1_out, I0);
  and and_4 (and_4_out, and_1_out, not_1_out);
  and and_5 (and_5_out, and_2_out, AC0);
  and and_6 (and_6_out, and_1_out, I1);
  and and_7 (and_7_out, and_1_out, not_2_out);
  and and_8 (and_8_out, and_5_out, AC1);
  and and_9 (and_9_out, and_1_out, I2);
  and and_10 (and_10_out, and_1_out, not_3_out);
  and and_11 (and_11_out, and_8_out, AC2);
  and and_12 (and_12_out, and_1_out, I3);
  and and_13 (and_13_out, and_1_out, not_4_out);
  and and_14 (and_14_out, and_11_out, AC3);
  and and_15 (and_15_out, and_1_out, I4);
  and and_16 (and_16_out, and_1_out, not_5_out);
  and and_17 (and_17_out, and_14_out, AC4);
  and and_18 (and_18_out, and_1_out, I5);
  and and_19 (and_19_out, and_1_out, not_6_out);
  and and_20 (and_20_out, and_17_out, AC5);
  and and_21 (and_21_out, and_1_out, I6);
  and and_22 (and_22_out, and_1_out, not_7_out);
  and and_23 (and_23_out, and_20_out, AC6);
  and and_24 (and_24_out, and_1_out, I7);
  and and_25 (and_25_out, and_1_out, not_8_out);
  and and_26 (and_26_out, and_23_out, AC7);
  and and_27 (and_27_out, and_1_out, I8);
  and and_28 (and_28_out, and_1_out, not_9_out);
  and and_29 (and_29_out, and_26_out, AC8);
  and and_30 (and_30_out, and_1_out, I9);
  and and_31 (and_31_out, and_1_out, not_10_out);
  and and_32 (and_32_out, and_29_out, AC9);
  and and_33 (and_33_out, and_1_out, I10);
  and and_34 (and_34_out, and_1_out, not_11_out);
  and and_35 (and_35_out, and_32_out, AC10);
  and and_36 (and_36_out, and_1_out, I11);
  and and_37 (and_37_out, and_1_out, not_12_out);
  and and_38 (and_38_out, and_35_out, AC11);
  and and_39 (and_39_out, and_1_out, I12);
  and and_40 (and_40_out, and_1_out, not_13_out);
  and and_41 (and_41_out, and_38_out, AC12);
  and and_42 (and_42_out, and_1_out, I13);
  and and_43 (and_43_out, and_1_out, not_14_out);
  and and_44 (and_44_out, and_41_out, AC13);
  and and_45 (and_45_out, and_1_out, I14);
  and and_46 (and_46_out, and_1_out, not_15_out);
  and and_47 (and_47_out, and_44_out, AC14);
  and and_48 (and_48_out, and_1_out, I15);
  and and_49 (and_49_out, and_1_out, not_16_out);
  and and_50 (output_carry, and_47_out, AC15);
  or or_1 (or_1_out, and_2_out, and_3_out);
  or or_2 (or_2_out, CLR, and_4_out);
  or or_3 (or_3_out, and_5_out, and_6_out);
  or or_4 (or_4_out, CLR, and_7_out);
  or or_5 (or_5_out, and_8_out, and_9_out);
  or or_6 (or_6_out, CLR, and_10_out);
  or or_7 (or_7_out, and_11_out, and_12_out);
  or or_8 (or_8_out, CLR, and_13_out);
  or or_9 (or_9_out, and_14_out, and_15_out);
  or or_10 (or_10_out, CLR, and_16_out);
  or or_11 (or_11_out, and_17_out, and_18_out);
  or or_12 (or_12_out, CLR, and_19_out);
  or or_13 (or_13_out, and_20_out, and_21_out);
  or or_14 (or_14_out, CLR, and_22_out);
  or or_15 (or_15_out, and_23_out, and_24_out);
  or or_16 (or_16_out, CLR, and_25_out);
  or or_17 (or_17_out, and_26_out, and_27_out);
  or or_18 (or_18_out, CLR, and_28_out);
  or or_19 (or_19_out, and_29_out, and_30_out);
  or or_20 (or_20_out, CLR, and_31_out);
  or or_21 (or_21_out, and_32_out, and_33_out);
  or or_22 (or_22_out, CLR, and_34_out);
  or or_23 (or_23_out, and_35_out, and_36_out);
  or or_24 (or_24_out, CLR, and_37_out);
  or or_25 (or_25_out, and_38_out, and_39_out);
  or or_26 (or_26_out, CLR, and_40_out);
  or or_27 (or_27_out, and_41_out, and_42_out);
  or or_28 (or_28_out, CLR, and_43_out);
  or or_29 (or_29_out, and_44_out, and_45_out);
  or or_30 (or_30_out, CLR, and_46_out);
  or or_31 (or_31_out, and_47_out, and_48_out);
  or or_32 (or_32_out, CLR, and_49_out);
  J_K_Flip_Flop j_k_ff_1 (.J(or_1_out), .clk(Clock), .K(or_2_out), .Q(AC0), .en(Enable));  // open: Qn, preset, reset
  J_K_Flip_Flop j_k_ff_2 (.J(or_3_out), .clk(Clock), .K(or_4_out), .Q(AC1), .en(Enable));  // open: Qn, preset, reset
  J_K_Flip_Flop j_k_ff_3 (.J(or_5_out), .clk(Clock), .K(or_6_out), .Q(AC2), .en(Enable));  // open: Qn, preset, reset
  J_K_Flip_Flop j_k_ff_4 (.J(or_7_out), .clk(Clock), .K(or_8_out), .Q(AC3), .en(Enable));  // open: Qn, preset, reset
  J_K_Flip_Flop j_k_ff_5 (.J(or_9_out), .clk(Clock), .K(or_10_out), .Q(AC4), .en(Enable));  // open: Qn, preset, reset
  J_K_Flip_Flop j_k_ff_6 (.J(or_11_out), .clk(Clock), .K(or_12_out), .Q(AC5), .en(Enable));  // open: Qn, preset, reset
  J_K_Flip_Flop j_k_ff_7 (.J(or_13_out), .clk(Clock), .K(or_14_out), .Q(AC6), .en(Enable));  // open: Qn, preset, reset
  J_K_Flip_Flop j_k_ff_8 (.J(or_15_out), .clk(Clock), .K(or_16_out), .Q(AC7), .en(Enable));  // open: Qn, preset, reset
  J_K_Flip_Flop j_k_ff_9 (.J(or_17_out), .clk(Clock), .K(or_18_out), .Q(AC8), .en(Enable));  // open: Qn, preset, reset
  J_K_Flip_Flop j_k_ff_10 (.J(or_19_out), .clk(Clock), .K(or_20_out), .Q(AC9), .en(Enable));  // open: Qn, preset, reset
  J_K_Flip_Flop j_k_ff_11 (
    .J(or_21_out), .clk(Clock), .K(or_22_out), .Q(AC10), .en(Enable));  // open: Qn, preset, reset
  J_K_Flip_Flop j_k_ff_12 (
    .J(or_23_out), .clk(Clock), .K(or_24_out), .Q(AC11), .en(Enable));  // open: Qn, preset, reset
  J_K_Flip_Flop j_k_ff_13 (
    .J(or_25_out), .clk(Clock), .K(or_26_out), .Q(AC12), .en(Enable));  // open: Qn, preset, reset
  J_K_Flip_Flop j_k_ff_14 (
    .J(or_27_out), .clk(Clock), .K(or_28_out), .Q(AC13), .en(Enable));  // open: Qn, preset, reset
  J_K_Flip_Flop j_k_ff_15 (
    .J(or_29_out), .clk(Clock), .K(or_30_out), .Q(AC14), .en(Enable));  // open: Qn, preset, reset
  J_K_Flip_Flop j_k_ff_16 (
    .J(or_31_out), .clk(Clock), .K(or_32_out), .Q(AC15), .en(Enable));  // open: Qn, preset, reset
endmodule
