// Logisim project ALU.circ as structural Verilog: 1 circuit, main circuit main
module main (
  input  AC_i,
  input  AND,
  input  DR_i,
  input  C_i_1,
  input  ADD,
  input  DDR,
  input  SUB,
  input  XOR,
  input  OR,
  input  COM,
  input  SHR,
  input  AC_i_1,
  input  SHL,
  input  AC_i_1_2,
  output Y,
  output c_out
);

  wire ADD_out, adder_1_out, and_1_out, AND_2_out, COM_out, DDR_out, not_1_out, or_1_out, OR_2_out, SHL_out,
       SHR_out, SUB_out, subtractor_1_out, xor_1_out, XOR_2_out;

  or or_1 (or_1_out, AC_i, DR_i);
  xor xor_1 (xor_1_out, AC_i, DR_i);
  not not_1 (not_1_out, AC_i);
  Subtractor #(.width(1)) subtractor_1 (.a(AC_i), .b(DR_i), .out(subtractor_1_out), .bin(AC_i_1));  // open: bout
  and and_1 (and_1_out, DR_i, AC_i);
  Adder #(.width(1)) adder_1 (.a(DR_i), .b(AC_i), .out(adder_1_out), .cin(C_i_1), .cout(c_out));
  and AND_2 (AND_2_out, AND, and_1_out);
  and u_ADD (ADD_out, ADD, adder_1_out);
  and u_DDR (DDR_out, DDR, DR_i);
  and XOR_2 (XOR_2_out, XOR, xor_1_out);
  and u_COM (COM_out, COM, not_1_out);
  and u_SHR (SHR_out, SHR, AC_i_1);
  and u_SHL (SHL_out, SHL, AC_i_1_2);
  and u_SUB (SUB_out, SUB, subtractor_1_out);
  and OR_2 (OR_2_out, OR, or_1_out);
  or or_3 (Y, AND_2_out, ADD_out, DDR_out, XOR_2_out, OR_2_out, COM_out, SHR_out, SHL_out, SUB_out);
endmodule
