// Logisim project ALU_FINAL.circ as structural Verilog: 1 circuit, main circuit main
module main (
  input  [15:0] DR,
  input  E_IN,
  input  [15:0] AC_IN,
  input  AND,
  input  ADD,
  input  DDR,
  input  XOR,
  input  COM,
  input  SHR,
  input  SHL,
  input  SUB,
  input  OR,
  output [15:0] AC_OUT,
  output E_OUT,
  output AC_LD
);

  ALU_MAIN_main main_1 (
    .E(E_IN), .AC0(AC_IN[0]), .AC1(AC_IN[1]), .AC2(AC_IN[2]), .AC3(AC_IN[3]), .AC4(AC_IN[4]), .AC5(AC_IN[5]),
    .AC6(AC_IN[6]), .AC7(AC_IN[7]), .AC8(AC_IN[8]), .AC9(AC_IN[9]), .AC10(AC_IN[10]), .AC11(AC_IN[11]),
    .AC12(AC_IN[12]), .AC13(AC_IN[13]), .AC14(AC_IN[14]), .AC15(AC_IN[15]), .DR(DR), .AND(AND), .ADD(ADD),
    .DDR(DDR), .XOR(XOR), .COM(COM), .SHR(SHR), .SHL(SHL), .SUB(SUB), .OR(OR), ._0(AC_OUT[0]),
    ._1(AC_OUT[1]), ._2(AC_OUT[2]), ._3(AC_OUT[3]), ._4(AC_OUT[4]), ._5(AC_OUT[5]), ._6(AC_OUT[6]),
    ._7(AC_OUT[7]), ._8(AC_OUT[8]), ._9(AC_OUT[9]), ._10(AC_OUT[10]), ._11(AC_OUT[11]), ._12(AC_OUT[12]),
    ._13(AC_OUT[13]), ._14(AC_OUT[14]), ._15(AC_OUT[15]), .E_2(E_OUT));
  or or_1 (AC_LD, OR, SUB, SHL, SHR, COM, XOR, DDR, ADD, AND);
endmodule
