// Logisim project ALU_MAIN.circ as structural Verilog: 1 circuit, main circuit main
module main (
  input  [15:0] DR,
  input  E,
  input  AC0,
  input  AC1,
  input  AC2,
  input  AC3,
  input  AC4,
  input  AC5,
  input  AC6,
  input  AC7,
  input  AC8,
  input  AC9,
  input  AC10,
  input  AC11,
  input  AC12,
  input  AC13,
  input  AC14,
  input  AC15,
  input  AND,
  input  ADD,
  input  DDR,
  input  XOR,
  input  COM,
  input  SHR,
  input  SHL,
  input  SUB,
  input  OR,
  output _0,
  output _1,
  output _2,
  output _3,
  output _4,
  output _5,
  output _6,
  output _7,
  output _8,
  output _9,
  output _10,
  output _11,
  output _12,
  output _13,
  output _14,
  output _15,
  output E_2
);

  wire main_1_c_out, main_2_c_out, main_3_c_out, main_4_c_out, main_5_c_out, main_6_c_out, main_7_c_out,
       main_8_c_out, main_9_c_out, main_10_c_out, main_11_c_out, main_12_c_out, main_13_c_out, main_14_c_out,
       main_15_c_out;

  ALU_main main_1 (
    .AND(AND), .DR_i(DR[0]), .C_i_1(E), .ADD(ADD), .DDR(DDR), .XOR(XOR), .OR(OR), .COM(COM), .SHR(SHR),
    .AC_i_1(AC1), .SHL(SHL), .AC_i_1_2(E), .AC_i(AC0), .Y(_0), .c_out(main_1_c_out), .SUB(SUB));
  ALU_main main_2 (
    .AND(AND), .DR_i(DR[1]), .C_i_1(main_1_c_out), .ADD(ADD), .DDR(DDR), .XOR(XOR), .OR(OR), .COM(COM),
    .SHR(SHR), .AC_i_1(AC2), .SHL(SHL), .AC_i_1_2(AC0), .AC_i(AC1), .Y(_1), .c_out(main_2_c_out), .SUB(SUB));
  ALU_main main_3 (
    .AND(AND), .DR_i(DR[2]), .C_i_1(main_2_c_out), .ADD(ADD), .DDR(DDR), .XOR(XOR), .OR(OR), .COM(COM),
    .SHR(SHR), .AC_i_1(AC3), .SHL(SHL), .AC_i_1_2(AC1), .AC_i(AC2), .Y(_2), .c_out(main_3_c_out), .SUB(SUB));
  ALU_main main_4 (
    .AND(AND), .DR_i(DR[3]), .C_i_1(main_3_c_out), .ADD(ADD), .DDR(DDR), .XOR(XOR), .OR(OR), .COM(COM),
    .SHR(SHR), .AC_i_1(AC4), .SHL(SHL), .AC_i_1_2(AC2), .AC_i(AC3), .Y(_3), .c_out(main_4_c_out), .SUB(SUB));
  ALU_main main_5 (
    .AND(AND), .DR_i(DR[4]), .C_i_1(main_4_c_out), .ADD(ADD), .DDR(DDR), .XOR(XOR), .OR(OR), .COM(COM),
    .SHR(SHR), .AC_i_1(AC5), .SHL(SHL), .AC_i_1_2(AC3), .AC_i(AC4), .Y(_4), .c_out(main_5_c_out), .SUB(SUB));
  ALU_main main_6 (
    .AND(AND), .DR_i(DR[5]), .C_i_1(main_5_c_out), .ADD(ADD), .DDR(DDR), .XOR(XOR), .OR(OR), .COM(COM),
    .SHR(SHR), .AC_i_1(AC6), .SHL(SHL), .AC_i_1_2(AC4), .AC_i(AC5), .Y(_5), .c_out(main_6_c_out), .SUB(SUB));
  ALU_main main_7 (
    .AND(AND), .DR_i(DR[6]), .C_i_1(main_6_c_out), .ADD(ADD), .DDR(DDR), .XOR(XOR), .OR(OR), .COM(COM),
    .SHR(SHR), .AC_i_1(AC7), .SHL(SHL), .AC_i_1_2(AC5), .AC_i(AC6), .Y(_6), .c_out(main_7_c_out), .SUB(SUB));
  ALU_main main_8 (
    .AND(AND), .DR_i(DR[7]), .C_i_1(main_7_c_out), .ADD(AND), .DDR(DDR), .XOR(XOR), .OR(OR), .COM(COM),
    .SHR(SHR), .AC_i_1(AC8), .SHL(SHL), .AC_i_1_2(AC6), .AC_i(AC7), .Y(_7), .c_out(main_8_c_out), .SUB(SUB));
  ALU_main main_9 (
    .AND(AND), .DR_i(DR[8]), .C_i_1(main_8_c_out), .ADD(ADD), .DDR(DDR), .XOR(XOR), .OR(OR), .COM(COM),
    .SHR(SHR), .AC_i_1(AC9), .SHL(SHL), .AC_i_1_2(AC7), .AC_i(AC8), .Y(_8), .c_out(main_9_c_out), .SUB(SUB));
  ALU_main main_10 (
    .AND(AND), .DR_i(DR[9]), .C_i_1(main_9_c_out), .ADD(ADD), .DDR(DDR), .XOR(XOR), .OR(OR), .COM(COM),
    .SHR(SHR), .AC_i_1(AC10), .SHL(SHL), .AC_i_1_2(AC8), .AC_i(AC9), .Y(_9), .c_out(main_10_c_out), .SUB(SUB));
  ALU_main main_11 (
    .AND(AND), .DR_i(DR[10]), .C_i_1(main_10_c_out), .ADD(ADD), .DDR(DDR), .XOR(XOR), .OR(OR), .COM(COM),
    .SHR(SHR), .AC_i_1(AC11), .SHL(SHL), .AC_i_1_2(AC9), .AC_i(AC10), .Y(_10), .c_out(main_11_c_out),
    .SUB(SUB));
  ALU_main main_12 (
    .AND(AND), .DR_i(DR[11]), .C_i_1(main_11_c_out), .ADD(ADD), .DDR(DDR), .XOR(XOR), .OR(OR), .COM(COM),
    .SHR(SHR), .AC_i_1(AC12), .SHL(SHL), .AC_i_1_2(AC10), .AC_i(AC11), .Y(_11), .c_out(main_12_c_out));  // open: SUB
  ALU_main main_13 (
    .AND(AND), .DR_i(DR[12]), .C_i_1(main_12_c_out), .ADD(ADD), .DDR(DDR), .XOR(XOR), .OR(OR), .COM(COM),
    .SHR(SHR), .AC_i_1(AC13), .SHL(SHL), .AC_i_1_2(AC11), .AC_i(AC12), .Y(_12), .c_out(main_13_c_out),
    .SUB(SUB));
  ALU_main main_14 (
    .AND(AND), .DR_i(DR[13]), .C_i_1(main_13_c_out), .ADD(ADD), .DDR(DDR), .XOR(XOR), .OR(OR), .COM(COM),
    .SHR(SHR), .AC_i_1(AC14), .SHL(SHL), .AC_i_1_2(AC12), .AC_i(AC13), .Y(_13), .c_out(main_14_c_out),
    .SUB(SUB));
  ALU_main main_15 (
    .AND(AND), .DR_i(DR[14]), .C_i_1(main_14_c_out), .ADD(ADD), .DDR(DDR), .XOR(XOR), .OR(OR), .COM(COM),
    .SHR(SHR), .AC_i_1(AC15), .SHL(SHL), .AC_i_1_2(AC13), .AC_i(AC14), .Y(_14), .c_out(main_15_c_out),
    .SUB(SUB));
  ALU_main main_16 (
    .AND(AND), .DR_i(DR[15]), .C_i_1(main_15_c_out), .ADD(ADD), .DDR(DDR), .XOR(XOR), .OR(OR), .COM(COM),
    .SHR(SHR), .AC_i_1(E), .SHL(SHL), .AC_i_1_2(AC14), .AC_i(AC14), .Y(_15), .c_out(E_2), .SUB(SUB));
endmodule
