// Logisim project COMPUTER 2.circ as structural Verilog: 1 circuit, main circuit main
module main (
);

  wire clock_1_out, main_1_add, main_1_and, main_1_artpc, main_1_clrac, main_1_com, main_1_drtac,
       main_1_drtar, main_1_incac, main_1_incdr, main_1_incpc, main_1_ld_ar, main_1_ld_dr, main_1_or,
       main_1_read, main_1_shl, main_1_shr, main_1_sub, main_1_write, main_1_xor, main_2_p11, main_2_p12,
       main_3_s, main_3_z;
  wire [1:0] main_1_actdr;
  wire [10:0] AR_q, DR_q, multiplexer_1_out, PC_q;
  wire [15:0] bit_extender_1_out, main_2_p10, main_2_p13, multiplexer_2_out, ram_1_data;
  wire [15:11] DR_q_2;

  Multiplexer #(.width(11)) multiplexer_1 (
    .in0(PC_q), .in1(DR_q), .out(multiplexer_1_out), .sel(main_1_drtar), .en(1'b1));
  Register #(.width(11)) AR (.D(multiplexer_1_out), .en(main_1_ld_ar), .Q(AR_q), .clk(clock_1_out));  // open: clr
  CONTROL_UNIT_main main_1 (
    .S(main_3_s), .Z(main_3_z), .INSTRUCTION_CODE({DR_q_2, DR_q}), .in_4(clock_1_out), .ADD(main_1_add),
    .CLRAC(main_1_clrac), .INCAC(main_1_incac), .DRTAC(main_1_drtac), .DRTAR(main_1_drtar),
    .WRITE(main_1_write), .SUB(main_1_sub), .OR(main_1_or), .AND(main_1_and), .READ(main_1_read),
    .ACTDR(main_1_actdr[0]), .INCDR(main_1_incdr), .PCTDR(main_1_actdr[1]), .XOR(main_1_xor),
    .COM(main_1_com), .SHL(main_1_shl), .SHR(main_1_shr), .INCPC(main_1_incpc), .ARTPC(main_1_artpc),
    .LD_AR(main_1_ld_ar), .LD_DR(main_1_ld_dr));  // open: NOP, PCTAR, NOP_2, NOP_3, RESV
  Counter #(.width(11), .max('h7ff)) PC (
    .load(main_1_artpc), .D(AR_q), .count(main_1_incpc), .Q(PC_q), .clk(clock_1_out));  // open: carry, clr
  assign bit_extender_1_out = {{5{1'b0}}, PC_q};  // Bit_Extender bit_extender_1
  RAM #(.addrWidth(11), .dataWidth(16), .bus("separate")) ram_1 (
    .addr(AR_q), .din({DR_q_2, DR_q}), .data(ram_1_data), .str(main_1_write), .sel(1'b1), .clk(clock_1_out),
    .ld(main_1_read));  // open: clr
  Multiplexer #(.select(2), .width(16)) multiplexer_2 (
    .in0(ram_1_data), .in1(main_2_p10), .in2(bit_extender_1_out), .out(multiplexer_2_out),
    .sel(main_1_actdr), .en(1'b1));  // open: in3
  Counter #(.width(16), .max('hffff)) DR (
    .load(main_1_ld_dr), .D(multiplexer_2_out), .count(main_1_incdr), .Q({DR_q_2, DR_q}), .clk(clock_1_out));  // open: carry, clr
  // ALU_FINAL_main main_2: pin names not known; wires that end beside it: main_1_or, main_1_and, main_1_add, main_1_drtac, main_1_xor, main_1_com, main_1_shr, main_1_shl, main_1_sub, main_2_p10, main_2_p11, main_2_p12, main_2_p13, {DR_q_2, DR_q}
  Counter #(.width(16), .max('hffff)) AC (
    .load(main_1_drtac), .D(main_2_p13), .count(main_1_incac), .Q(main_2_p10), .clk(clock_1_out),
    .clr(main_1_clrac));  // open: carry
  S_AND_Z_main main_3 (.AC(main_2_p10), .S(main_3_s), .Z(main_3_z));
  Clock clock_1 (.out(clock_1_out));
  D_Flip_Flop d_ff_1 (.clk(clock_1_out), .D(main_2_p11), .Q(main_2_p12), .preset(1'b0), .en(1'b1));  // open: Qn, reset
endmodule
