// Logisim project CONTROL_UNIT.circ as structural Verilog: 1 circuit, main circuit main
module main (
  input  [15:0] INSTRUCTION_CODE,
  input  S,
  input  Z,
  input  in_4,
  output NOP,
  output ADD,
  output CLRAC,
  output INCAC,
  output DRTAC,
  output DRTAR,
  output PCTAR,
  output WRITE,
  output NOP_2,
  output SUB,
  output OR,
  output AND,
  output READ,
  output ACTDR,
  output INCDR,
  output PCTDR,
  output NOP_3,
  output XOR,
  output COM,
  output SHL,
  output SHR,
  output INCPC,
  output ARTPC,
  output RESV,
  output LD_AR,
  output LD_DR
);

  wire INP_LOGIC_load_sbr, MAP_LOGIC_out_2, multiplexer_1_out;
  wire [1:0] INP_LOGIC_s0, rom_1_data_4;
  wire [2:0] rom_1_data, rom_1_data_2;
  wire [6:0] CAR_q, INCREAMENTER_s0, MAP_LOGIC_out, multiplexer_2_out, SBR_q;
  wire [16:0] rom_1_data_3;

  INPUT_LOGIC_main INP_LOGIC (
    .I0(rom_1_data_3[7]), .I1(rom_1_data_3[8]), .T(multiplexer_1_out), .S0(INP_LOGIC_s0[0]),
    .S1(INP_LOGIC_s0[1]), .LOAD_SBR(INP_LOGIC_load_sbr));
  Multiplexer #(.select(2), .enable("false")) multiplexer_1 (
    .in0(1'b1), .in1(MAP_LOGIC_out_2), .in2(S), .in3(Z), .out(multiplexer_1_out), .sel(rom_1_data_4));
  mapping_logic_main MAP_LOGIC (.out_2(MAP_LOGIC_out_2), .Instruction_code(INSTRUCTION_CODE), .out(MAP_LOGIC_out));
  Multiplexer #(.select(2), .width(7)) multiplexer_2 (
    .in0(INCREAMENTER_s0), .in1(rom_1_data_3[6:0]), .in2(SBR_q), .in3(MAP_LOGIC_out),
    .out(multiplexer_2_out), .sel(INP_LOGIC_s0), .en(1'b1));
  Register #(.width(7)) CAR (.D(multiplexer_2_out), .en(1'b1), .Q(CAR_q), .clk(in_4));  // open: clr
  ROM #(.addrWidth(7), .dataWidth(20)) rom_1 (
    .addr(CAR_q), .data({rom_1_data, rom_1_data_3[16:14], rom_1_data_2, rom_1_data_4, rom_1_data_3[8:0]}),
    .sel(1'b1));
  INCREAMENTER_main INCREAMENTER (
    .S6(INCREAMENTER_s0[6]), .S5(INCREAMENTER_s0[5]), .S4(INCREAMENTER_s0[4]), .S3(INCREAMENTER_s0[3]),
    .S2(INCREAMENTER_s0[2]), .S1(INCREAMENTER_s0[1]), .S0(INCREAMENTER_s0[0]), .A6(CAR_q[6]), .A5(CAR_q[5]),
    .A4(CAR_q[4]), .A3(CAR_q[3]), .A2(CAR_q[2]), .A1(CAR_q[1]), .A0(CAR_q[0]));  // open: CARRY
  Register #(.width(7)) SBR (.D(INCREAMENTER_s0), .en(INP_LOGIC_load_sbr), .Q(SBR_q), .clk(in_4));  // open: clr
  Decoder #(.select(3), .enable("false")) decoder_1 (
    .out0(NOP), .out1(ADD), .out2(CLRAC), .out3(INCAC), .out4(DRTAC), .out5(DRTAR), .out6(PCTAR),
    .out7(WRITE), .sel(rom_1_data));
  Decoder #(.select(3), .enable("false")) decoder_2 (
    .out0(NOP_2), .out1(SUB), .out2(OR), .out3(AND), .out4(READ), .out5(ACTDR), .out6(INCDR), .out7(PCTDR),
    .sel(rom_1_data_3[16:14]));
  Decoder #(.select(3), .enable("false")) decoder_3 (
    .out0(NOP_3), .out1(XOR), .out2(COM), .out3(SHL), .out4(SHR), .out5(INCPC), .out6(ARTPC), .out7(RESV),
    .sel(rom_1_data_2));
  or or_1 (LD_AR, DRTAR, PCTAR);
  or or_2 (LD_DR, ACTDR, READ, PCTDR);

  // Notes on the sheet:
  //   contents of rom_1 (hex, n*v repeats v):
  //   2c3 10002 20040 40 406 40 2c3 3040 2c3 1400a e0040 40 2c3 1000e 9400f e0040 2c3 1000e 80040 40 2c3
  //   10002 4040 40 2c3 10002 8040 40 2c3 10002 c040 40 2c3 10002 840 40 2c3 10002 1040 40 2c3 10002 1840
  //   40 2c3 10002 2040 40 16*0 c0041 12842 a0180 10044 a0100
  //   F1
  //   F2
  //   F3
endmodule
