// Logisim project INCREAMENTER.circ as structural Verilog: 1 circuit, main circuit main
module main (
  input  A6,
  input  A5,
  input  A4,
  input  A3,
  input  A2,
  input  A1,
  input  A0,
  output CARRY,
  output S6,
  output S5,
  output S4,
  output S3,
  output S2,
  output S1,
  output S0
);

  wire HA_2_p3, HA_2_p4, HA_4_p4, HA_5_p4, HA_6_p4, HA_p4;

  // HA_main HA: pin names not known; wires that end beside it: S6, A6, CARRY, HA_p4
  // HA_main HA_2: pin names not known; wires that end beside it: S4, A4, HA_2_p3, HA_2_p4
  // HA_main HA_3: pin names not known; wires that end beside it: S5, A5, HA_p4, HA_2_p3
  // HA_main HA_4: pin names not known; wires that end beside it: S3, A3, HA_2_p4, HA_4_p4
  // HA_main HA_5: pin names not known; wires that end beside it: S2, A2, HA_4_p4, HA_5_p4
  // HA_main HA_6: pin names not known; wires that end beside it: S1, A1, HA_5_p4, HA_6_p4
  // HA_main HA_7: pin names not known; wires that end beside it: S0, A0, HA_6_p4, 1'b1
endmodule
