// Logisim project INPUT LOGIC.circ as structural Verilog: 1 circuit, main circuit main
module main (
  input  I0,
  input  I1,
  input  T,
  output S0,
  output S1,
  output LOAD_SBR
);

  wire and_1_out, and_2_out, and_3_out, not_1_out, not_2_out, not_3_out;

  not not_1 (not_1_out, T);
  not not_2 (not_2_out, I1);
  not not_3 (not_3_out, I0);
  and and_1 (and_1_out, not_2_out, not_3_out, T);
  and and_2 (and_2_out, not_2_out, I0, T);
  and and_3 (and_3_out, I1, I0);
  and and_4 (LOAD_SBR, I0, not_2_out, T);
  or or_1 (S0, and_1_out, and_2_out, and_3_out);

  assign S1 = I1;
endmodule
