// Logisim project S_AND_Z.circ as structural Verilog: 1 circuit, main circuit main
module main (
  input  [15:0] AC,
  output S,
  output Z
);

  or or_1 (Z, AC[15], AC[14], AC[13], AC[12], AC[11], AC[10], AC[9], AC[8], AC[7], AC[6], AC[5], AC[4], AC[3], AC[2], AC[1], AC[0]);

  assign S = AC[15];
endmodule
