// Logisim project mapping logic.circ as structural Verilog: 1 circuit, main circuit main
module main (
  input  [15:0] Instruction_code,
  output out_2,
  output [6:0] out
);


  assign out = {1'b0, Instruction_code[14:11], 2'b00};
  assign out_2 = Instruction_code[15];
endmodule
